// Logisim project Car Alarm.circ as structural Verilog: 1 circuit, main circuit main
module main (
  input  M,
  input  D,
  input  V,
  output A
);

  wire AND_out, Clock_out, OR_out;

  Clock Clock (.out(Clock_out));
  and AND (AND_out, M, OR_out);
  or OR (OR_out, D, V, A);
  D_Flip_Flop D_Flip_Flop (.clk(Clock_out), .D(AND_out), .Q(A));  // open: Qn, preset, en, reset
endmodule
