// Logisim project StateMachine.circ as structural Verilog: 1 circuit, main circuit main
module main (
  input  In,
  output Out
);


  // Notes on the sheet:
  //   A SIMPLE STATE MACHINE
  //   INPUT SECTION: Do not change anything here!
  //   You may only change the values of the inputs for testing using the hand tool.
  //   Do not introduce any other input or output pins in the circuit.
  //   To your logic
  //   OUTPUT SECTION: Do not change anything here!
  //   Do not introduce any other input or output pins in the circuit.
  //   From your logic
endmodule
